// Digital circuit frontpanel.dig as structural Verilog
module frontpanel (
  input  [15:0] A,
  input  [7:0] SD,
  input  [15:0] A_2,
  input  [15:0] A_3,
  input  [15:0] A_4,
  input  [7:0] SD_2,
  input  [7:0] SD_3,
  input  [7:0] SD_4,
  output [15:0] R0,
  output [15:0] R1,
  output [15:0] R2,
  output [15:0] R3,
  output [15:0] B
);

  wire button_1_out, decoder_1_p2, decoder_1_p3, decoder_1_p4, execute_1_p3;
  wire [1:0] PC_out;
  wire [31:0] multiplexer_1_out;

  Counter #(.Bits(2)) PC (.en(1'b1), .C(button_1_out), .clr(1'b0), .out(PC_out));  // open: ovf
  Button button_1 (.out(button_1_out));
  Multiplexer #(.Selector_Bits(2), .Bits(32)) multiplexer_1 (
    .sel(PC_out), .in_0({{8{1'b0}}, SD, A}), .in_1({{8{1'b0}}, SD_2, A_2}), .in_2({{8{1'b0}}, SD_3, A_3}),
    .in_3({{8{1'b0}}, SD_4, A_4}), .out(multiplexer_1_out));
  // decoder decoder_1: pin names not known; wires that end beside it: multiplexer_1_out, decoder_1_p2, decoder_1_p3, decoder_1_p4
  // execute execute_1: pin names not known; wires that end beside it: decoder_1_p2, B, execute_1_p3
  // regfile regfile_1: pin names not known; wires that end beside it: decoder_1_p3, decoder_1_p4, execute_1_p3, button_1_out, B, R0, R1, R2, R3

  // Notes on the sheet:
  //   A: default 100
  //   SD: default 1
  //   A_2: default 200
  //   A_3: default 99
  //   A_4: default 34
  //   SD_2: default 18
  //   SD_3: default 35
  //   SD_4: default 48
endmodule
